// Logisim project SAP-1.circ as structural Verilog: 13 circuits, main circuit reg_b
module main (
  input  in_1,
  input  in_2,
  input  in_3,
  input  clk,
  input  in_5,
  input  in_6,
  input  in_7,
  input  in_8,
  input  in_9,
  input  in_10,
  input  in_11,
  input  in_12,
  input  [7:0] in_13,
  input  in_14,
  output [3:0] out_15,
  output [7:0] reg_a_out,
  output [7:0] alu_out,
  output [7:0] reg_c_out,
  output [7:0] out_19,
  output [7:0] out_20,
  output [7:0] out_21,
  output [7:0] out_22,
  output [7:0] reg_b_out,
  output [7:0] out_24,
  output [7:0] out_25,
  output [7:0] out_26,
  output [7:0] out_27,
  output [7:0] out_28,
  output [7:0] out_29,
  output [7:0] out_30,
  output [7:0] out_31,
  output [7:0] out_32,
  output [7:0] out_33,
  output [7:0] out_34,
  output [7:0] out_35,
  output [3:0] out_36,
  output [3:0] out_37,
  output [7:0] out_38
);

  wire a_in, b_in, ins_reg_in_en, ins_reg_out_en, mar_in_en, or_1_out, or_2_out, pc_en, pc_out, sram_rd,
       sram_wr;

  or or_1 (or_1_out, mar_in_en, in_9);
  or or_2 (or_2_out, sram_wr, in_6);
  pc pc_1 (.pc_en(pc_en), .pc_clk(in_12), .pc_reset(in_10), .pc_out_en(pc_out), .pc_val(out_15), .pc_out(alu_out[3:0]));
  sram sram_1 (
    .sram_rd(sram_rd), .sram_wr(or_2_out), .sram_d_in(alu_out), .mar_d_in(alu_out), .mar_in_en(or_1_out),
    .sram_clk(in_12), .sram_d_out(alu_out), .out_8(out_19), .out_9(out_20), .out_10(out_21), .out_11(out_22),
    .out_12(out_24), .out_13(out_25), .out_14(out_26), .out_15(out_27), .out_16(out_28), .out_17(out_29),
    .out_18(out_30), .out_19(out_31), .out_20(out_32), .out_21(out_33), .out_22(out_34), .out_23(out_35));
  assign alu_out = in_11 ? in_13 : 8'bz;  // Controlled_Buffer controlled_buffer_1
  reg_a reg_a_1 (
    .reg_in(alu_out), .reg_in_en(a_in), .reg_clk(in_12), .reg_out_en(in_8), .reg_int_out(reg_a_out),
    .reg_out(alu_out));
  reg_b reg_b_1 (
    .reg_in(alu_out), .reg_in_en(b_in), .reg_clk(in_12), .reg_out_en(in_5), .reg_int_out(reg_b_out),
    .reg_out(alu_out));
  Ins_reg ins_reg_1 (
    .ins_reg_in(alu_out), .ins_reg_in_en(ins_reg_in_en), .clk(in_12), .ins_reg_out_en(ins_reg_out_en),
    .add_outs(alu_out[3:0]), .ins_out(out_37));
  alu alu_1 (
    .alu_in_1(reg_a_out), .alu_out_en(in_1), .alu_sub(in_2), .alu_in_2(reg_b_out), .alu_out(alu_out));  // open: alu_carry_out
  cntrl_seq cntrl_seq_1 (
    .CLK(in_12), .reset(in_14), .D(out_37[3]), .C(out_37[2]), .B(out_37[1]), .A(out_37[0]), .a_in(a_in),
    .b_in(b_in), .pc_en(pc_en), .ins_in(ins_reg_in_en), .ram_rd(sram_rd), .ins_out(ins_reg_out_en),
    .pc_out(pc_out), .mar_in(mar_in_en), .alu_out(in_1), .ram_wr(sram_wr));  // open: HLT
  reg_c reg_c_1 (
    .reg_in(alu_out), .reg_in_en(in_3), .reg_clk(clk), .reg_out_en(in_7), .reg_int_out(reg_c_out));  // open: reg_out

  assign out_36 = alu_out[3:0];
  assign out_38 = alu_out;

  // Other names for the same wires on the sheet: a_out = in_8; alu_out_t = in_1; alu_sub = in_2; b_out = in_5;
  //   clk_t = in_12; debug = in_11; debug_data[7:0] = in_13; pc_reset = in_10
endmodule

module reg_b (
  input  [7:0] reg_in,
  input  reg_in_en,
  input  reg_clk,
  input  reg_out_en,
  output [7:0] reg_int_out,
  output [7:0] reg_out
);

  wire multiplexer_1_out, multiplexer_2_out, multiplexer_3_out, multiplexer_4_out, multiplexer_5_out,
       multiplexer_6_out, multiplexer_7_out, multiplexer_8_out;

  Multiplexer multiplexer_1 (.in0(reg_int_out[7]), .in1(reg_in[7]), .out(multiplexer_1_out), .sel(reg_in_en));
  D_Flip_Flop d_ff_1 (.D(multiplexer_1_out), .clk(reg_clk), .Q(reg_int_out[7]));  // open: Qn, preset, reset
  assign reg_out[7] = reg_out_en ? reg_int_out[7] : 1'bz;  // Controlled_Buffer controlled_buffer_1
  Multiplexer multiplexer_2 (.in0(reg_int_out[6]), .in1(reg_in[6]), .out(multiplexer_2_out), .sel(reg_in_en));
  D_Flip_Flop d_ff_2 (.D(multiplexer_2_out), .clk(reg_clk), .Q(reg_int_out[6]));  // open: Qn, preset, reset
  assign reg_out[6] = reg_out_en ? reg_int_out[6] : 1'bz;  // Controlled_Buffer controlled_buffer_2
  Multiplexer multiplexer_3 (.in0(reg_int_out[5]), .in1(reg_in[5]), .out(multiplexer_3_out), .sel(reg_in_en));
  D_Flip_Flop d_ff_3 (.D(multiplexer_3_out), .clk(reg_clk), .Q(reg_int_out[5]));  // open: Qn, preset, reset
  assign reg_out[5] = reg_out_en ? reg_int_out[5] : 1'bz;  // Controlled_Buffer controlled_buffer_3
  Multiplexer multiplexer_4 (.in0(reg_int_out[4]), .in1(reg_in[4]), .out(multiplexer_4_out), .sel(reg_in_en));
  D_Flip_Flop d_ff_4 (.D(multiplexer_4_out), .clk(reg_clk), .Q(reg_int_out[4]));  // open: Qn, preset, reset
  assign reg_out[4] = reg_out_en ? reg_int_out[4] : 1'bz;  // Controlled_Buffer controlled_buffer_4
  Multiplexer multiplexer_5 (.in0(reg_int_out[3]), .in1(reg_in[3]), .out(multiplexer_5_out), .sel(reg_in_en));
  D_Flip_Flop d_ff_5 (.D(multiplexer_5_out), .clk(reg_clk), .Q(reg_int_out[3]));  // open: Qn, preset, reset
  assign reg_out[3] = reg_out_en ? reg_int_out[3] : 1'bz;  // Controlled_Buffer controlled_buffer_5
  Multiplexer multiplexer_6 (.in0(reg_int_out[2]), .in1(reg_in[2]), .out(multiplexer_6_out), .sel(reg_in_en));
  D_Flip_Flop d_ff_6 (.D(multiplexer_6_out), .clk(reg_clk), .Q(reg_int_out[2]));  // open: Qn, preset, reset
  assign reg_out[2] = reg_out_en ? reg_int_out[2] : 1'bz;  // Controlled_Buffer controlled_buffer_6
  Multiplexer multiplexer_7 (.in0(reg_int_out[1]), .in1(reg_in[1]), .out(multiplexer_7_out), .sel(reg_in_en));
  D_Flip_Flop d_ff_7 (.D(multiplexer_7_out), .clk(reg_clk), .Q(reg_int_out[1]));  // open: Qn, preset, reset
  assign reg_out[1] = reg_out_en ? reg_int_out[1] : 1'bz;  // Controlled_Buffer controlled_buffer_7
  Multiplexer multiplexer_8 (.in0(reg_int_out[0]), .in1(reg_in[0]), .out(multiplexer_8_out), .sel(reg_in_en));
  D_Flip_Flop d_ff_8 (.D(multiplexer_8_out), .clk(reg_clk), .Q(reg_int_out[0]));  // open: Qn, preset, reset
  assign reg_out[0] = reg_out_en ? reg_int_out[0] : 1'bz;  // Controlled_Buffer controlled_buffer_8

  // Notes on the sheet:
  //   input
  //   input control
  //   clock
  //   output control
  //   memory
  //   internal output
  //   output
endmodule

module alu (
  input  [7:0] alu_in_1,
  input  alu_out_en,
  input  alu_sub,
  input  [7:0] alu_in_2,
  output [7:0] alu_out,
  output alu_carry_out
);

  wire adder_2_cout, adder_3_cout, adder_4_cout, adder_5_cout, adder_6_cout, adder_7_cout, adder_8_cout,
       xor_1_out, xor_2_out, xor_3_out, xor_4_out, xor_5_out, xor_6_out, xor_7_out, xor_8_out;
  wire [7:0] adder_8_out;

  xor xor_1 (xor_1_out, alu_in_2[7], alu_sub);
  Adder #(.width(1)) adder_1 (
    .a(alu_in_1[7]), .b(xor_1_out), .out(adder_8_out[7]), .cin(adder_2_cout), .cout(alu_carry_out));
  xor xor_2 (xor_2_out, alu_in_2[6], alu_sub);
  Adder #(.width(1)) adder_2 (
    .a(alu_in_1[6]), .b(xor_2_out), .out(adder_8_out[6]), .cin(adder_3_cout), .cout(adder_2_cout));
  Adder #(.width(1)) adder_3 (
    .a(alu_in_1[5]), .b(xor_3_out), .out(adder_8_out[5]), .cin(adder_4_cout), .cout(adder_3_cout));
  xor xor_3 (xor_3_out, alu_in_2[5], alu_sub);
  xor xor_4 (xor_4_out, alu_in_2[4], alu_sub);
  Adder #(.width(1)) adder_4 (
    .a(alu_in_1[4]), .b(xor_4_out), .out(adder_8_out[4]), .cin(adder_5_cout), .cout(adder_4_cout));
  xor xor_5 (xor_5_out, alu_in_2[3], alu_sub);
  Adder #(.width(1)) adder_5 (
    .a(alu_in_1[3]), .b(xor_5_out), .out(adder_8_out[3]), .cin(adder_6_cout), .cout(adder_5_cout));
  xor xor_6 (xor_6_out, alu_in_2[2], alu_sub);
  Adder #(.width(1)) adder_6 (
    .a(alu_in_1[2]), .b(xor_6_out), .out(adder_8_out[2]), .cin(adder_7_cout), .cout(adder_6_cout));
  Adder #(.width(1)) adder_7 (
    .a(alu_in_1[1]), .b(xor_7_out), .out(adder_8_out[1]), .cin(adder_8_cout), .cout(adder_7_cout));
  xor xor_7 (xor_7_out, alu_in_2[1], alu_sub);
  xor xor_8 (xor_8_out, alu_in_2[0], alu_sub);
  Adder #(.width(1)) adder_8 (.a(alu_in_1[0]), .b(xor_8_out), .out(adder_8_out[0]), .cin(alu_sub), .cout(adder_8_cout));
  assign alu_out = alu_out_en ? adder_8_out : 8'bz;  // Controlled_Buffer controlled_buffer_1

  // Notes on the sheet:
  //   input 1
  //   carry out
  //   subtract control
  //   full adders
  //   output control
  //   input 2
  //   alu output
endmodule

module decodr (
  input  [3:0] dec_sel,
  output [15:0] dec_out
);

  wire not_1_out, not_2_out, not_3_out, not_4_out;

  not not_1 (not_1_out, dec_sel[3]);
  not not_2 (not_2_out, dec_sel[2]);
  not not_3 (not_3_out, dec_sel[1]);
  not not_4 (not_4_out, dec_sel[0]);
  and and_1 (dec_out[0], not_4_out, not_3_out, not_2_out, not_1_out);
  and and_2 (dec_out[1], dec_sel[0], not_3_out, not_2_out, not_1_out);
  and and_3 (dec_out[2], not_4_out, dec_sel[1], not_2_out, not_1_out);
  and and_4 (dec_out[3], dec_sel[0], dec_sel[1], not_2_out, not_1_out);
  and and_5 (dec_out[4], not_4_out, not_3_out, dec_sel[2], not_1_out);
  and and_6 (dec_out[5], dec_sel[0], not_3_out, dec_sel[2], not_1_out);
  and and_7 (dec_out[6], not_4_out, dec_sel[1], dec_sel[2], not_1_out);
  and and_8 (dec_out[7], dec_sel[0], dec_sel[1], dec_sel[2], not_1_out);
  and and_9 (dec_out[8], not_4_out, not_3_out, not_2_out, dec_sel[3]);
  and and_10 (dec_out[9], dec_sel[0], not_3_out, not_2_out, dec_sel[3]);
  and and_11 (dec_out[10], not_4_out, dec_sel[1], not_2_out, dec_sel[3]);
  and and_12 (dec_out[11], dec_sel[0], dec_sel[1], not_2_out, dec_sel[3]);
  and and_13 (dec_out[12], not_4_out, not_3_out, dec_sel[2], dec_sel[3]);
  and and_14 (dec_out[13], dec_sel[0], not_3_out, dec_sel[2], dec_sel[3]);
  and and_15 (dec_out[14], not_4_out, dec_sel[1], dec_sel[2], dec_sel[3]);
  and and_16 (dec_out[15], dec_sel[0], dec_sel[1], dec_sel[2], dec_sel[3]);
endmodule

module sramcell (
  input  [7:0] data_in,
  input  wr_in,
  input  clk,
  input  cs,
  input  rd_en,
  output [7:0] memory_content,
  output [7:0] data_out
);

  wire and_1_out, and_2_out;

  and and_1 (and_1_out, wr_in, cs);
  and and_2 (and_2_out, cs, rd_en);
  reg_b reg_b_1 (
    .reg_in(data_in), .reg_in_en(and_1_out), .reg_clk(clk), .reg_out_en(and_2_out),
    .reg_int_out(memory_content), .reg_out(data_out));
endmodule

module sram (
  input  sram_rd,
  input  sram_wr,
  input  [7:0] sram_d_in,
  input  [7:0] mar_d_in,
  input  mar_in_en,
  input  sram_clk,
  output [7:0] sram_d_out,
  output [7:0] out_8,
  output [7:0] out_9,
  output [7:0] out_10,
  output [7:0] out_11,
  output [7:0] out_12,
  output [7:0] out_13,
  output [7:0] out_14,
  output [7:0] out_15,
  output [7:0] out_16,
  output [7:0] out_17,
  output [7:0] out_18,
  output [7:0] out_19,
  output [7:0] out_20,
  output [7:0] out_21,
  output [7:0] out_22,
  output [7:0] out_23
);

  wire [7:0] controlled_buffer_1_out, reg_b_1_reg_int_out;
  wire [15:0] decodr_1_dec_out;

  reg_b reg_b_1 (
    .reg_in(mar_d_in), .reg_in_en(mar_in_en), .reg_clk(sram_clk), .reg_int_out(reg_b_1_reg_int_out));  // open: reg_out_en, reg_out
  decodr decodr_1 (.dec_sel(reg_b_1_reg_int_out[3:0]), .dec_out(decodr_1_dec_out));
  assign controlled_buffer_1_out = sram_wr ? sram_d_in : 8'bz;  // Controlled_Buffer controlled_buffer_1
  sramcell sramcell_1 (
    .data_in(controlled_buffer_1_out), .wr_in(sram_wr), .clk(sram_clk), .cs(decodr_1_dec_out[0]),
    .rd_en(sram_rd), .memory_content(out_8), .data_out(controlled_buffer_1_out));
  sramcell sramcell_2 (
    .data_in(controlled_buffer_1_out), .wr_in(sram_wr), .clk(sram_clk), .cs(decodr_1_dec_out[1]),
    .rd_en(sram_rd), .memory_content(out_9), .data_out(controlled_buffer_1_out));
  sramcell sramcell_3 (
    .data_in(controlled_buffer_1_out), .wr_in(sram_wr), .clk(sram_clk), .cs(decodr_1_dec_out[2]),
    .rd_en(sram_rd), .memory_content(out_10), .data_out(controlled_buffer_1_out));
  sramcell sramcell_4 (
    .data_in(controlled_buffer_1_out), .wr_in(sram_wr), .clk(sram_clk), .cs(decodr_1_dec_out[3]),
    .rd_en(sram_rd), .memory_content(out_11), .data_out(controlled_buffer_1_out));
  sramcell sramcell_5 (
    .data_in(controlled_buffer_1_out), .wr_in(sram_wr), .clk(sram_clk), .cs(decodr_1_dec_out[4]),
    .rd_en(sram_rd), .memory_content(out_12), .data_out(controlled_buffer_1_out));
  sramcell sramcell_6 (
    .data_in(controlled_buffer_1_out), .wr_in(sram_wr), .clk(sram_clk), .cs(decodr_1_dec_out[5]),
    .rd_en(sram_rd), .memory_content(out_13), .data_out(controlled_buffer_1_out));
  sramcell sramcell_7 (
    .data_in(controlled_buffer_1_out), .wr_in(sram_wr), .clk(sram_clk), .cs(decodr_1_dec_out[6]),
    .rd_en(sram_rd), .memory_content(out_14), .data_out(controlled_buffer_1_out));
  sramcell sramcell_8 (
    .data_in(controlled_buffer_1_out), .wr_in(sram_wr), .clk(sram_clk), .cs(decodr_1_dec_out[7]),
    .rd_en(sram_rd), .memory_content(out_15), .data_out(controlled_buffer_1_out));
  sramcell sramcell_9 (
    .data_in(controlled_buffer_1_out), .wr_in(sram_wr), .clk(sram_clk), .cs(decodr_1_dec_out[8]),
    .rd_en(sram_rd), .memory_content(out_16), .data_out(controlled_buffer_1_out));
  sramcell sramcell_10 (
    .data_in(controlled_buffer_1_out), .wr_in(sram_wr), .clk(sram_clk), .cs(decodr_1_dec_out[9]),
    .rd_en(sram_rd), .memory_content(out_17), .data_out(controlled_buffer_1_out));
  sramcell sramcell_11 (
    .data_in(controlled_buffer_1_out), .wr_in(sram_wr), .clk(sram_clk), .cs(decodr_1_dec_out[10]),
    .rd_en(sram_rd), .memory_content(out_18), .data_out(controlled_buffer_1_out));
  sramcell sramcell_12 (
    .data_in(controlled_buffer_1_out), .wr_in(sram_wr), .clk(sram_clk), .cs(decodr_1_dec_out[11]),
    .rd_en(sram_rd), .memory_content(out_19), .data_out(controlled_buffer_1_out));
  sramcell sramcell_13 (
    .data_in(controlled_buffer_1_out), .wr_in(sram_wr), .clk(sram_clk), .cs(decodr_1_dec_out[12]),
    .rd_en(sram_rd), .memory_content(out_20), .data_out(controlled_buffer_1_out));
  sramcell sramcell_14 (
    .data_in(controlled_buffer_1_out), .wr_in(sram_wr), .clk(sram_clk), .cs(decodr_1_dec_out[13]),
    .rd_en(sram_rd), .memory_content(out_21), .data_out(controlled_buffer_1_out));
  sramcell sramcell_15 (
    .data_in(controlled_buffer_1_out), .wr_in(sram_wr), .clk(sram_clk), .cs(decodr_1_dec_out[14]),
    .rd_en(sram_rd), .memory_content(out_22), .data_out(controlled_buffer_1_out));
  sramcell sramcell_16 (
    .data_in(controlled_buffer_1_out), .wr_in(sram_wr), .clk(sram_clk), .cs(decodr_1_dec_out[15]),
    .rd_en(sram_rd), .memory_content(out_23), .data_out(controlled_buffer_1_out));
  assign sram_d_out = sram_rd ? controlled_buffer_1_out : 8'bz;  // Controlled_Buffer controlled_buffer_2
endmodule

module Ins_reg (
  input  [7:0] ins_reg_in,
  input  ins_reg_in_en,
  input  clk,
  input  ins_reg_out_en,
  output [3:0] add_outs,
  output [3:0] ins_out
);

  wire [3:0] reg_b_1_reg_int_out;

  reg_b reg_b_1 (
    .reg_in(ins_reg_in), .reg_in_en(ins_reg_in_en), .reg_clk(clk),
    .reg_int_out({ins_out, reg_b_1_reg_int_out}));  // open: reg_out_en, reg_out
  assign add_outs = ins_reg_out_en ? reg_b_1_reg_int_out : 4'bz;  // Controlled_Buffer controlled_buffer_1
endmodule

module pc (
  input  pc_en,
  input  pc_clk,
  input  pc_reset,
  input  pc_out_en,
  output [3:0] pc_val,
  output [3:0] pc_out
);

  wire j_k_ff_2_qn, j_k_ff_3_qn, j_k_ff_4_qn;

  J_K_Flip_Flop j_k_ff_1 (
    .J(pc_en), .K(pc_en), .clk(j_k_ff_2_qn), .Q(pc_val[3]), .reset(pc_reset));  // open: Qn, preset
  J_K_Flip_Flop j_k_ff_2 (
    .J(pc_en), .K(pc_en), .clk(j_k_ff_3_qn), .Q(pc_val[2]), .Qn(j_k_ff_2_qn), .reset(pc_reset));  // open: preset
  J_K_Flip_Flop j_k_ff_3 (
    .J(pc_en), .K(pc_en), .clk(j_k_ff_4_qn), .Q(pc_val[1]), .Qn(j_k_ff_3_qn), .reset(pc_reset));  // open: preset
  J_K_Flip_Flop j_k_ff_4 (
    .J(pc_en), .K(pc_en), .clk(pc_clk), .Q(pc_val[0]), .Qn(j_k_ff_4_qn), .reset(pc_reset));  // open: preset
  assign pc_out = pc_out_en ? pc_val : 4'bz;  // Controlled_Buffer controlled_buffer_1

  // Notes on the sheet:
  //   clock
  //   reset
  //   output control
  //   count control
  //   counter output
endmodule

module cntrl_seq (
  input  CLK,
  input  reset,
  input  D,
  input  C,
  input  B,
  input  A,
  output a_in,
  output b_in,
  output pc_en,
  output ins_in,
  output ram_rd,
  output ins_out,
  output pc_out,
  output HLT,
  output mar_in,
  output alu_out,
  output ram_wr
);

  wire and_1_out, and_3_out, and_5_out, and_6_out, and_7_out, and_8_out, ins_decoder_1_add,
       ins_decoder_1_lda, ins_decoder_1_ldb, ins_decoder_1_sub, ring_cntr_1_t4, ring_cntr_1_t5,
       ring_cntr_1_t6;

  ring_cntr ring_cntr_1 (
    .CLK(CLK), .reset(reset), .T6(ring_cntr_1_t6), .T1(pc_out), .T2(ins_in), .T3(pc_en), .T4(ring_cntr_1_t4),
    .T5(ring_cntr_1_t5));
  ins_decoder ins_decoder_1 (
    .D(D), .C(C), .B(B), .A(A), .LDA(ins_decoder_1_lda), .LDB(ins_decoder_1_ldb), .SUB(ins_decoder_1_sub),
    .ADD(ins_decoder_1_add), .HLT(HLT));  // open: O_U_T
  and and_1 (and_1_out, ins_decoder_1_lda, ring_cntr_1_t4);
  and and_2 (a_in, ins_decoder_1_lda, ring_cntr_1_t5);
  and and_3 (and_3_out, ins_decoder_1_ldb, ring_cntr_1_t4);
  and and_4 (b_in, ins_decoder_1_ldb, ring_cntr_1_t5);
  and and_5 (and_5_out, ring_cntr_1_t4, ins_decoder_1_sub);
  and and_6 (and_6_out, ring_cntr_1_t5, ins_decoder_1_sub);
  or or_1 (ram_wr, and_6_out, and_8_out);
  and and_7 (and_7_out, ring_cntr_1_t4, ins_decoder_1_add);
  or or_2 (ram_rd, b_in, a_in, ins_in);
  or or_3 (alu_out, and_6_out, and_8_out);
  and and_8 (and_8_out, ring_cntr_1_t5, ins_decoder_1_add);
  or or_4 (ins_out, and_1_out, and_5_out, and_7_out, and_3_out);
  or or_5 (mar_in, and_1_out, pc_out, and_7_out, and_5_out, and_3_out);
endmodule

module ring_cntr (
  input  CLK,
  input  reset,
  output T6,
  output T1,
  output T2,
  output T3,
  output T4,
  output T5
);

  wire nor_1_out;

  nor nor_1 (nor_1_out, T6, T5, T4, T3, T2, T1);
  D_Flip_Flop d_ff_1 (.D(nor_1_out), .clk(CLK), .Q(T1), .reset(reset));  // open: Qn, preset
  D_Flip_Flop d_ff_2 (.D(T1), .clk(CLK), .Q(T2), .reset(reset));  // open: Qn, preset
  D_Flip_Flop d_ff_3 (.D(T2), .clk(CLK), .Q(T3), .reset(reset));  // open: Qn, preset
  D_Flip_Flop d_ff_4 (.D(T3), .clk(CLK), .Q(T4), .reset(reset));  // open: Qn, preset
  D_Flip_Flop d_ff_5 (.D(T4), .clk(CLK), .Q(T5));  // open: Qn, preset, reset
  D_Flip_Flop d_ff_6 (.D(T5), .clk(CLK), .Q(T6), .reset(reset));  // open: Qn, preset
endmodule

module ins_decoder (
  input  D,
  input  C,
  input  B,
  input  A,
  output LDA,
  output LDB,
  output SUB,
  output ADD,
  output O_U_T,
  output HLT
);

  wire not_1_out, not_2_out, not_3_out, not_4_out;

  not not_1 (not_1_out, D);
  not not_2 (not_2_out, C);
  not not_3 (not_3_out, B);
  not not_4 (not_4_out, A);
  and and_1 (LDA, D, not_2_out, B, A);
  and and_2 (LDB, not_1_out, C, not_3_out, A);
  and and_3 (SUB, not_1_out, C, B, A);
  and and_4 (ADD, D, C, not_3_out, A);
  and and_5 (O_U_T, not_1_out, not_2_out, not_3_out, not_4_out);
  and and_6 (HLT, not_1_out, C, not_3_out, not_4_out);
endmodule

module reg_a (
  input  [7:0] reg_in,
  input  reg_in_en,
  input  reg_clk,
  input  reg_out_en,
  output [7:0] reg_int_out,
  output [7:0] reg_out
);

  wire multiplexer_1_out, multiplexer_2_out, multiplexer_3_out, multiplexer_4_out, multiplexer_5_out,
       multiplexer_6_out, multiplexer_7_out, multiplexer_8_out;

  Multiplexer multiplexer_1 (.in0(reg_int_out[7]), .in1(reg_in[7]), .out(multiplexer_1_out), .sel(reg_in_en));
  D_Flip_Flop d_ff_1 (.D(multiplexer_1_out), .clk(reg_clk), .Q(reg_int_out[7]));  // open: Qn, preset, reset
  assign reg_out[7] = reg_out_en ? reg_int_out[7] : 1'bz;  // Controlled_Buffer controlled_buffer_1
  Multiplexer multiplexer_2 (.in0(reg_int_out[6]), .in1(reg_in[6]), .out(multiplexer_2_out), .sel(reg_in_en));
  D_Flip_Flop d_ff_2 (.D(multiplexer_2_out), .clk(reg_clk), .Q(reg_int_out[6]));  // open: Qn, preset, reset
  assign reg_out[6] = reg_out_en ? reg_int_out[6] : 1'bz;  // Controlled_Buffer controlled_buffer_2
  Multiplexer multiplexer_3 (.in0(reg_int_out[5]), .in1(reg_in[5]), .out(multiplexer_3_out), .sel(reg_in_en));
  D_Flip_Flop d_ff_3 (.D(multiplexer_3_out), .clk(reg_clk), .Q(reg_int_out[5]));  // open: Qn, preset, reset
  assign reg_out[5] = reg_out_en ? reg_int_out[5] : 1'bz;  // Controlled_Buffer controlled_buffer_3
  Multiplexer multiplexer_4 (.in0(reg_int_out[4]), .in1(reg_in[4]), .out(multiplexer_4_out), .sel(reg_in_en));
  D_Flip_Flop d_ff_4 (.D(multiplexer_4_out), .clk(reg_clk), .Q(reg_int_out[4]));  // open: Qn, preset, reset
  assign reg_out[4] = reg_out_en ? reg_int_out[4] : 1'bz;  // Controlled_Buffer controlled_buffer_4
  Multiplexer multiplexer_5 (.in0(reg_int_out[3]), .in1(reg_in[3]), .out(multiplexer_5_out), .sel(reg_in_en));
  D_Flip_Flop d_ff_5 (.D(multiplexer_5_out), .clk(reg_clk), .Q(reg_int_out[3]));  // open: Qn, preset, reset
  assign reg_out[3] = reg_out_en ? reg_int_out[3] : 1'bz;  // Controlled_Buffer controlled_buffer_5
  Multiplexer multiplexer_6 (.in0(reg_int_out[2]), .in1(reg_in[2]), .out(multiplexer_6_out), .sel(reg_in_en));
  D_Flip_Flop d_ff_6 (.D(multiplexer_6_out), .clk(reg_clk), .Q(reg_int_out[2]));  // open: Qn, preset, reset
  assign reg_out[2] = reg_out_en ? reg_int_out[2] : 1'bz;  // Controlled_Buffer controlled_buffer_6
  Multiplexer multiplexer_7 (.in0(reg_int_out[1]), .in1(reg_in[1]), .out(multiplexer_7_out), .sel(reg_in_en));
  D_Flip_Flop d_ff_7 (.D(multiplexer_7_out), .clk(reg_clk), .Q(reg_int_out[1]));  // open: Qn, preset, reset
  assign reg_out[1] = reg_out_en ? reg_int_out[1] : 1'bz;  // Controlled_Buffer controlled_buffer_7
  Multiplexer multiplexer_8 (.in0(reg_int_out[0]), .in1(reg_in[0]), .out(multiplexer_8_out), .sel(reg_in_en));
  D_Flip_Flop d_ff_8 (.D(multiplexer_8_out), .clk(reg_clk), .Q(reg_int_out[0]));  // open: Qn, preset, reset
  assign reg_out[0] = reg_out_en ? reg_int_out[0] : 1'bz;  // Controlled_Buffer controlled_buffer_8

  // Notes on the sheet:
  //   input
  //   input control
  //   clock
  //   output control
  //   memory
  //   internal output
  //   output
endmodule

module reg_c (
  input  [7:0] reg_in,
  input  reg_in_en,
  input  reg_clk,
  input  reg_out_en,
  output [7:0] reg_int_out,
  output [7:0] reg_out
);

  wire multiplexer_1_out, multiplexer_2_out, multiplexer_3_out, multiplexer_4_out, multiplexer_5_out,
       multiplexer_6_out, multiplexer_7_out, multiplexer_8_out;

  Multiplexer multiplexer_1 (.in0(reg_int_out[7]), .in1(reg_in[7]), .out(multiplexer_1_out), .sel(reg_in_en));
  D_Flip_Flop d_ff_1 (.D(multiplexer_1_out), .clk(reg_clk), .Q(reg_int_out[7]));  // open: Qn, preset, reset
  assign reg_out[7] = reg_out_en ? reg_int_out[7] : 1'bz;  // Controlled_Buffer controlled_buffer_1
  Multiplexer multiplexer_2 (.in0(reg_int_out[6]), .in1(reg_in[6]), .out(multiplexer_2_out), .sel(reg_in_en));
  D_Flip_Flop d_ff_2 (.D(multiplexer_2_out), .clk(reg_clk), .Q(reg_int_out[6]));  // open: Qn, preset, reset
  assign reg_out[6] = reg_out_en ? reg_int_out[6] : 1'bz;  // Controlled_Buffer controlled_buffer_2
  Multiplexer multiplexer_3 (.in0(reg_int_out[5]), .in1(reg_in[5]), .out(multiplexer_3_out), .sel(reg_in_en));
  D_Flip_Flop d_ff_3 (.D(multiplexer_3_out), .clk(reg_clk), .Q(reg_int_out[5]));  // open: Qn, preset, reset
  assign reg_out[5] = reg_out_en ? reg_int_out[5] : 1'bz;  // Controlled_Buffer controlled_buffer_3
  Multiplexer multiplexer_4 (.in0(reg_int_out[4]), .in1(reg_in[4]), .out(multiplexer_4_out), .sel(reg_in_en));
  D_Flip_Flop d_ff_4 (.D(multiplexer_4_out), .clk(reg_clk), .Q(reg_int_out[4]));  // open: Qn, preset, reset
  assign reg_out[4] = reg_out_en ? reg_int_out[4] : 1'bz;  // Controlled_Buffer controlled_buffer_4
  Multiplexer multiplexer_5 (.in0(reg_int_out[3]), .in1(reg_in[3]), .out(multiplexer_5_out), .sel(reg_in_en));
  D_Flip_Flop d_ff_5 (.D(multiplexer_5_out), .clk(reg_clk), .Q(reg_int_out[3]));  // open: Qn, preset, reset
  assign reg_out[3] = reg_out_en ? reg_int_out[3] : 1'bz;  // Controlled_Buffer controlled_buffer_5
  Multiplexer multiplexer_6 (.in0(reg_int_out[2]), .in1(reg_in[2]), .out(multiplexer_6_out), .sel(reg_in_en));
  D_Flip_Flop d_ff_6 (.D(multiplexer_6_out), .clk(reg_clk), .Q(reg_int_out[2]));  // open: Qn, preset, reset
  assign reg_out[2] = reg_out_en ? reg_int_out[2] : 1'bz;  // Controlled_Buffer controlled_buffer_6
  Multiplexer multiplexer_7 (.in0(reg_int_out[1]), .in1(reg_in[1]), .out(multiplexer_7_out), .sel(reg_in_en));
  D_Flip_Flop d_ff_7 (.D(multiplexer_7_out), .clk(reg_clk), .Q(reg_int_out[1]));  // open: Qn, preset, reset
  assign reg_out[1] = reg_out_en ? reg_int_out[1] : 1'bz;  // Controlled_Buffer controlled_buffer_7
  Multiplexer multiplexer_8 (.in0(reg_int_out[0]), .in1(reg_in[0]), .out(multiplexer_8_out), .sel(reg_in_en));
  D_Flip_Flop d_ff_8 (.D(multiplexer_8_out), .clk(reg_clk), .Q(reg_int_out[0]));  // open: Qn, preset, reset
  assign reg_out[0] = reg_out_en ? reg_int_out[0] : 1'bz;  // Controlled_Buffer controlled_buffer_8

  // Notes on the sheet:
  //   input
  //   input control
  //   clock
  //   output control
  //   memory
  //   internal output
  //   output
endmodule
